// Logisim project simulation.circ as structural Verilog: 2 circuits, main circuit main
module main (
);

  wire and_1_out, btn0, btn1, clk, clock_1_out, comparator_1_gt, comparator_2_lt, comparator_3_eq,
       comparator_4_gt, comparator_6_gt, cond_en, decoder_1_out0, decoder_1_out1, decoder_1_out2,
       decoder_2_out1, decoder_2_out2, decoder_2_out3, decoder_2_out4, decoder_2_out5, decoder_2_out6,
       decoder_2_out7, decoder_2_out10, decoder_2_out11, decoder_2_out12, decoder_2_out13, decoder_2_out14,
       decoder_2_out15, decoder_2_out16, decoder_2_out17, decoder_2_out18, decoder_2_out19, decoder_2_out30,
       decoder_2_out31, decoder_3_out0, decoder_3_out1, decoder_3_out2, decoder_3_out3, decoder_3_out4,
       decoder_3_out5, decoder_3_out6, decoder_3_out7, decoder_3_out8, decoder_3_out9, decoder_3_out10,
       decoder_3_out11, decoder_3_out12, decoder_3_out13, decoder_3_out14, decoder_3_out15, decoder_3_out16,
       decoder_3_out17, decoder_3_out18, decoder_3_out19, decoder_3_out20, decoder_3_out21, decoder_3_out22,
       decoder_3_out23, decoder_3_out24, decoder_3_out25, decoder_3_out26, decoder_3_out27, decoder_3_out28,
       decoder_3_out29, decoder_3_out30, decoder_3_out31, decoder_4_out0, decoder_4_out1, decoder_4_out2,
       decoder_4_out3, decoder_4_out4, decoder_4_out5, decoder_4_out6, decoder_4_out7, decoder_4_out8,
       decoder_4_out9, decoder_4_out10, decoder_4_out11, decoder_4_out12, decoder_4_out13, decoder_4_out14,
       decoder_4_out15, decoder_4_out16, decoder_4_out17, decoder_4_out18, decoder_4_out30, decoder_5_out0,
       decoder_5_out1, decoder_5_out2, decoder_5_out3, decoder_5_out4, decoder_5_out5, decoder_6_out0,
       decoder_6_out1, decoder_6_out2, decoder_6_out3, F_write, freeze, halt, Halted_qn, mem_write,
       multiplexer_2_out, multiplexer_4_out, not_1_out, not_2_out, or_1_out, or_2_out, or_4_out, or_5_out,
       or_6_out, port_write, priority_encoder_1_gs, SP_en, SP_inc, tty_en, write;
  wire [1:0] addr_mode, cond, write_op_sel;
  wire [2:0] adder_3_out, Instr_State_q, mode, multiplexer_7_out, multiplexer_8_out, write_sel;
  wire [2:2] subtractor_2_bout;
  wire [3:0] alu_1_flags_out, F, F_val, multiplexer_17_out, priority_encoder_1_out, read_sel;
  wire [3:2] adder_5_cout;
  wire [3:3] comparator_7_eq;
  wire [4:0] subtractor_3_out, subtractor_4_out;
  wire [7:0] A, adder_4_out, adder_5_out, alu_1_result, B_q, bit_extender_6_out, bit_extender_7_out,
       bit_extender_8_out, bit_extender_9_out, C0, C1, data, H, Instr_q, L, mem, mem_val, Memory_dout,
       multiplexer_5_out, multiplexer_6_out, multiplexer_11_out, multiplexer_14_out, multiplexer_15_out,
       multiplexer_19_out, multiplexer_20_out, multiplexer_21_out, negator_1_out, port_in, Program_data,
       random_1_out, shifter_1_out, SP, subtractor_1_out, subtractor_2_out;
  wire [7:2] multiplexer_10_out;
  wire [8:0] bit_extender_3_out, bit_extender_4_out, multiplier_1_out;
  wire [9:0] and_3_out, and_4_out, bit_extender_5_out, leds, not_3_out, or_3_out, shifter_2_out,
       shifter_3_out, shifter_4_out, switches;
  wire [15:0] adder_1_out, adder_2_out, bit_extender_1_out, bit_extender_2_out, multiplexer_1_out,
       multiplexer_3_out, multiplexer_9_out, PC;
  wire [23:0] Microcode_data, seven_seg;

  Register #(.width(16)) u_PC (.D(multiplexer_1_out), .en(or_1_out), .clk(clk), .Q(PC));  // open: clr
  Multiplexer #(.enable("false"), .width(16)) multiplexer_1 (
    .in0(adder_2_out), .in1(multiplexer_3_out), .out(multiplexer_1_out), .sel(Microcode_data[21]));
  or or_1 (or_1_out, comparator_3_eq, Microcode_data[21], Microcode_data[20]);
  Multiplexer #(.enable("false"), .select(2)) multiplexer_2 (
    .in0(F[3]), .in1(F[2]), .in2(F[1]), .in3(F[0]), .out(multiplexer_2_out), .sel(cond));
  Comparator #(.mode("unsigned")) comparator_1 (.a(data), .b({8{1'b0}}), .gt(comparator_1_gt));  // open: eq, lt
  Comparator #(.mode("unsigned")) comparator_2 (.a(data), .b({8{1'b1}}), .lt(comparator_2_lt));  // open: gt, eq
  Multiplexer #(.enable("false"), .select(2), .width(16)) multiplexer_3 (
    .in0({H, L}), .in1({C0, C1}), .in2(adder_1_out), .out(multiplexer_3_out), .sel(mode[1:0]));  // open: in3
  not not_1 (not_1_out, multiplexer_2_out);
  Multiplexer #(.enable("false"), .select(2)) multiplexer_4 (
    .in0(multiplexer_2_out), .in1(not_1_out), .in2(comparator_1_gt), .in3(comparator_2_lt),
    .out(multiplexer_4_out), .sel(mode[1:0]));
  assign bit_extender_1_out = {{8{data[7]}}, data};  // Bit_Extender bit_extender_1
  Adder #(.width(16)) adder_1 (.a(bit_extender_1_out), .b(PC), .out(adder_1_out));  // open: cin, cout
  Adder #(.width(16)) adder_2 (.a(PC), .b(16'h1), .out(adder_2_out));  // open: cin, cout
  and and_1 (and_1_out, cond_en, multiplexer_4_out);
  Negator negator_1 (.in(SP), .out(negator_1_out));
  Multiplexer #(.enable("false"), .width(8)) multiplexer_5 (
    .in0(H), .in1(C0), .out(multiplexer_5_out), .sel(addr_mode[0]));
  Multiplexer #(.enable("false"), .width(8)) multiplexer_6 (
    .in0(L), .in1(C1), .out(multiplexer_6_out), .sel(addr_mode[0]));
  D_Flip_Flop Halted (.D(halt), .clk(clk), .Qn(Halted_qn));  // open: Q, preset, reset
  TTY tty_1 (.data(data[6:0]), .clk(clk), .we(tty_en));  // open: clr
  Register Instr (.D(mem), .en(comparator_3_eq), .clk(clk), .Q(Instr_q));  // open: clr
  Register #(.width(3)) Instr_State (.D(multiplexer_7_out), .en(1'b1), .clk(clk), .Q(Instr_State_q));  // open: clr
  Multiplexer #(.enable("false"), .width(3)) multiplexer_7 (
    .in0(multiplexer_8_out), .in1(Instr_State_q), .out(multiplexer_7_out), .sel(freeze));
  Multiplexer #(.enable("false"), .width(3)) multiplexer_8 (
    .in0(adder_3_out), .in1(3'b000), .out(multiplexer_8_out), .sel(or_2_out));
  assign bit_extender_2_out = {{8{1'b1}}, negator_1_out};  // Bit_Extender bit_extender_2
  and and_2 (clk, Halted_qn, clock_1_out);
  Clock clock_1 (.out(clock_1_out));
  not not_2 (not_2_out, comparator_3_eq);
  or or_2 (or_2_out, and_1_out, Microcode_data[22]);
  // Probe on multiplexer_9_out
  Multiplexer #(.enable("false"), .select(2), .width(16)) multiplexer_9 (
    .in0(PC), .in1(bit_extender_2_out), .in2({multiplexer_5_out, multiplexer_6_out}),
    .in3({multiplexer_5_out, multiplexer_6_out}), .out(multiplexer_9_out), .sel(addr_mode));
  // Probe on {multiplexer_10_out, cond}
  Multiplexer #(.enable("false"), .width(8)) multiplexer_10 (
    .in0(mem), .in1(Instr_q), .out({multiplexer_10_out, cond}), .sel(not_2_out));
  Comparator #(.width(3)) comparator_3 (.a(Instr_State_q), .b(3'b000), .eq(comparator_3_eq));  // open: gt, lt
  Adder #(.width(3)) adder_3 (.a(Instr_State_q), .b(3'b001), .out(adder_3_out));  // open: cin, cout
  RAM #(.addrWidth(15), .enables("line")) Memory (
    .addr(multiplexer_9_out[14:0]), .we(mem_write), .clk(clk), .din(mem_val), .dout(Memory_dout));
  assign bit_extender_3_out = {{1{1'b0}}, shifter_1_out};  // Bit_Extender bit_extender_3
  Shifter #(.shift("lr")) shifter_1 (.in({multiplexer_10_out, cond}), .\dist (3'b010), .out(shifter_1_out));
  assign bit_extender_4_out = {{6{1'b0}}, Instr_State_q};  // Bit_Extender bit_extender_4
  LED led_1 (.in(leds[9]));
  Multiplier #(.width(9)) multiplier_1 (
    .a(bit_extender_3_out), .b(9'h6), .out(multiplier_1_out), .cin(bit_extender_4_out));  // open: cout
  Register #(.width(4)) u_F (.D(F_val), .en(F_write), .clk(clk), .Q(F));  // open: clr
  LED led_2 (.in(leds[8]));
  LED led_3 (.in(leds[7]));
  LED led_4 (.in(leds[6]));
  LED led_5 (.in(leds[5]));
  Button button_1 (.out(btn0));
  Button button_2 (.out(btn1));
  ROM #(.addrWidth(9), .dataWidth(24)) Microcode (
    .addr(multiplier_1_out),
    .data({Microcode_data[23:20], halt, cond_en, F_write, write, SP_inc, SP_en, mode, write_sel, read_sel, write_op_sel, Microcode_data[1:0]}));
  // Probe on F
  LED led_6 (.in(leds[4]));
  LED led_7 (.in(leds[3]));
  LED led_8 (.in(leds[2]));
  LED led_9 (.in(leds[1]));
  ROM #(.addrWidth(15)) Program (.addr(multiplexer_9_out[14:0]), .data(Program_data));
  LED led_10 (.in(leds[0]));
  Register u_SP (.D(multiplexer_11_out), .en(SP_en), .clk(clk), .Q(SP));  // open: clr
  Hex_Digit_Display hex_digit_display_1 (.value(seven_seg[23:20]));  // open: dp
  // DipSwitch #(.number(10)) dipswitch_1: pin names not known; wires that end beside it: switches[9], switches[8], switches[7], switches[6], switches[5], switches[4], switches[3], switches[2], switches[1], switches[0]
  // Probe on cond
  Hex_Digit_Display hex_digit_display_2 (.value(seven_seg[19:16]));  // open: dp
  Hex_Digit_Display hex_digit_display_3 (.value(seven_seg[15:12]));  // open: dp
  Adder adder_4 (.a(SP), .b(8'h1), .out(adder_4_out));  // open: cin, cout
  Multiplexer #(.enable("false"), .width(8)) multiplexer_11 (
    .in0(adder_4_out), .in1(subtractor_1_out), .out(multiplexer_11_out), .sel(SP_inc));
  Subtractor subtractor_1 (.a(SP), .b(8'h1), .out(subtractor_1_out));  // open: bin, bout
  Hex_Digit_Display hex_digit_display_4 (.value(seven_seg[11:8]));  // open: dp
  Hex_Digit_Display hex_digit_display_5 (.value(seven_seg[7:4]));  // open: dp
  // Probe on Microcode_data[1:0]
  Multiplexer #(.enable("false"), .width(2)) multiplexer_12 (
    .in0(Microcode_data[1:0]), .in1(2'b00), .out(addr_mode), .sel(comparator_3_eq));
  // Probe on write_op_sel
  // Probe on read_sel
  // Probe on write_sel
  // Probe on mode
  Multiplexer #(.enable("false"), .width(8)) multiplexer_13 (
    .in0(Program_data), .in1(Memory_dout), .out(mem), .sel(multiplexer_9_out[15]));
  Hex_Digit_Display hex_digit_display_6 (.value(seven_seg[3:0]));  // open: dp
  Decoder #(.select(2)) decoder_1 (
    .out0(decoder_1_out0), .out1(decoder_1_out1), .out2(decoder_1_out2), .sel(C0[6:5]), .en(port_write));  // open: out3
  Decoder #(.select(5)) decoder_2 (
    .out0(tty_en), .out1(decoder_2_out1), .out2(decoder_2_out2), .out3(decoder_2_out3),
    .out4(decoder_2_out4), .out5(decoder_2_out5), .out6(decoder_2_out6), .out7(decoder_2_out7),
    .out10(decoder_2_out10), .out11(decoder_2_out11), .out12(decoder_2_out12), .out13(decoder_2_out13),
    .out14(decoder_2_out14), .out15(decoder_2_out15), .out16(decoder_2_out16), .out17(decoder_2_out17),
    .out18(decoder_2_out18), .out19(decoder_2_out19), .out30(decoder_2_out30), .out31(decoder_2_out31),
    .sel(C0[4:0]), .en(decoder_1_out0));  // open: out8, out9, out20, out21, out22, out23, out24, out25, out26, out27, out28, out29
  Decoder #(.select(5)) decoder_3 (
    .out0(decoder_3_out0), .out1(decoder_3_out1), .out2(decoder_3_out2), .out3(decoder_3_out3),
    .out4(decoder_3_out4), .out5(decoder_3_out5), .out6(decoder_3_out6), .out7(decoder_3_out7),
    .out8(decoder_3_out8), .out9(decoder_3_out9), .out10(decoder_3_out10), .out11(decoder_3_out11),
    .out12(decoder_3_out12), .out13(decoder_3_out13), .out14(decoder_3_out14), .out15(decoder_3_out15),
    .out16(decoder_3_out16), .out17(decoder_3_out17), .out18(decoder_3_out18), .out19(decoder_3_out19),
    .out20(decoder_3_out20), .out21(decoder_3_out21), .out22(decoder_3_out22), .out23(decoder_3_out23),
    .out24(decoder_3_out24), .out25(decoder_3_out25), .out26(decoder_3_out26), .out27(decoder_3_out27),
    .out28(decoder_3_out28), .out29(decoder_3_out29), .out30(decoder_3_out30), .out31(decoder_3_out31),
    .sel(C0[4:0]), .en(decoder_1_out1));
  Decoder #(.select(5)) decoder_4 (
    .out0(decoder_4_out0), .out1(decoder_4_out1), .out2(decoder_4_out2), .out3(decoder_4_out3),
    .out4(decoder_4_out4), .out5(decoder_4_out5), .out6(decoder_4_out6), .out7(decoder_4_out7),
    .out8(decoder_4_out8), .out9(decoder_4_out9), .out10(decoder_4_out10), .out11(decoder_4_out11),
    .out12(decoder_4_out12), .out13(decoder_4_out13), .out14(decoder_4_out14), .out15(decoder_4_out15),
    .out16(decoder_4_out16), .out17(decoder_4_out17), .out18(decoder_4_out18), .out30(decoder_4_out30),
    .sel(C0[4:0]), .en(decoder_1_out2));  // open: out19, out20, out21, out22, out23, out24, out25, out26, out27, out28, out29, out31
  Priority_Encoder #(.select(4)) priority_encoder_1 (
    .in0(decoder_2_out10), .in1(decoder_2_out11), .in2(decoder_2_out12), .in3(decoder_2_out13),
    .in4(decoder_2_out14), .in5(decoder_2_out15), .in6(decoder_2_out16), .in7(decoder_2_out17),
    .in8(decoder_2_out18), .in9(decoder_2_out19), .out(priority_encoder_1_out), .gs(priority_encoder_1_gs),
    .en_in(1'b1));  // open: in10, in11, in12, in13, in14, in15, en_out
  Comparator #(.mode("unsigned")) comparator_4 (.a(data), .b({8{1'b0}}), .gt(comparator_4_gt));  // open: eq, lt
  Priority_Encoder #(.select(5)) priority_encoder_2 (
    .in0(decoder_3_out3), .in1(decoder_3_out4), .in2(decoder_3_out5), .in3(decoder_3_out6),
    .in4(decoder_3_out7), .in5(decoder_3_out8), .in6(decoder_3_out9), .in7(decoder_3_out10),
    .in8(decoder_3_out11), .in9(decoder_3_out12), .in10(decoder_3_out13), .in11(decoder_3_out14),
    .in12(decoder_3_out15), .in13(decoder_3_out16), .in14(decoder_3_out17), .in15(decoder_3_out18),
    .in16(decoder_3_out19), .in17(decoder_3_out20), .in18(decoder_3_out21), .in19(decoder_3_out22),
    .in20(decoder_3_out23), .in21(decoder_3_out24), .in22(decoder_3_out25), .in23(decoder_3_out26),
    .in24(decoder_3_out27), .in25(decoder_3_out28), .in26(decoder_3_out29), .in27(decoder_3_out30),
    .in28(decoder_3_out31), .in29(decoder_4_out0), .in30(decoder_4_out1), .in31(decoder_4_out2), .en_in(1'b1));  // open: out, gs, en_out
  Priority_Encoder #(.select(4)) priority_encoder_3 (
    .in0(decoder_4_out3), .in1(decoder_4_out4), .in2(decoder_4_out5), .in3(decoder_4_out6),
    .in4(decoder_4_out7), .in5(decoder_4_out8), .in6(decoder_4_out9), .in7(decoder_4_out10),
    .in8(decoder_4_out11), .in9(decoder_4_out12), .in10(decoder_4_out13), .in11(decoder_4_out14),
    .in12(decoder_4_out15), .in13(decoder_4_out16), .in14(decoder_4_out17), .in15(decoder_4_out18),
    .en_in(1'b1));  // open: out, gs, en_out
  Register register_1 ();  // open: D, en, clk, Q, clr
  Register #(.width(4)) register_2 (.D(data[3:0]), .en(decoder_2_out2), .clk(clk), .Q(seven_seg[3:0]));  // open: clr
  assign bit_extender_5_out = {{9{1'b0}}, comparator_4_gt};  // Bit_Extender bit_extender_5
  Decoder #(.select(3)) decoder_5 (
    .out0(decoder_5_out0), .out1(decoder_5_out1), .out2(decoder_5_out2), .out3(decoder_5_out3),
    .out4(decoder_5_out4), .out5(decoder_5_out5), .out6(mem_write), .out7(port_write), .sel(write_sel),
    .en(write));
  Register #(.width(4)) register_3 (.D(data[3:0]), .en(decoder_2_out3), .clk(clk), .Q(seven_seg[7:4]));  // open: clr
  assign not_3_out = ~shifter_2_out;  // NOT_Gate not_3, 10 bits wide
  Shifter #(.width(10)) shifter_2 (.in(10'h1), .\dist (priority_encoder_1_out), .out(shifter_2_out));
  Shifter #(.width(10)) shifter_3 (.in(bit_extender_5_out), .\dist (priority_encoder_1_out), .out(shifter_3_out));
  assign or_3_out = shifter_3_out | and_3_out;  // OR_Gate or_3, 10 bits wide
  assign and_3_out = not_3_out & leds;  // AND_Gate and_3, 10 bits wide
  Decoder #(.select(2)) decoder_6 (
    .out0(decoder_6_out0), .out1(decoder_6_out1), .out2(decoder_6_out2), .out3(decoder_6_out3), .sel(cond),
    .en(decoder_5_out1));
  Register #(.width(4)) register_4 (.D(data[3:0]), .en(decoder_2_out4), .clk(clk), .Q(seven_seg[11:8]));  // open: clr
  Register #(.width(10)) u_LEDs (.D(or_3_out), .en(priority_encoder_1_gs), .clk(clk), .Q(leds));  // open: clr
  Register u_A (.D(data), .en(or_4_out), .clk(clk), .Q(A));  // open: clr
  or or_4 (or_4_out, decoder_5_out0, decoder_6_out0);
  Register B (.D(data), .en(decoder_6_out1), .clk(clk), .Q(B_q));  // open: clr
  Register u_H (.D(data), .en(or_5_out), .clk(clk), .Q(H));  // open: clr
  or or_5 (or_5_out, decoder_6_out2, decoder_5_out2);
  Register u_L (.D(data), .en(or_6_out), .clk(clk), .Q(L));  // open: clr
  or or_6 (or_6_out, decoder_6_out3, decoder_5_out3);
  Register u_C0 (.D(data), .en(decoder_5_out4), .clk(clk), .Q(C0));  // open: clr
  Register u_C1 (.D(data), .en(decoder_5_out5), .clk(clk), .Q(C1));  // open: clr
  Register #(.width(4)) register_5 (.D(data[3:0]), .en(decoder_2_out5), .clk(clk), .Q(seven_seg[15:12]));  // open: clr
  assign mem_val = mem_write ? data : 8'bz;  // Controlled_Buffer controlled_buffer_1
  Register #(.width(4)) register_6 (.D(data[3:0]), .en(decoder_2_out6), .clk(clk), .Q(seven_seg[19:16]));  // open: clr
  Multiplexer #(.enable("false"), .select(2), .width(8)) multiplexer_14 (
    .in0(A), .in1(B_q), .in2(H), .in3(L), .out(multiplexer_14_out), .sel(cond));
  Register #(.width(4)) register_7 (.D(data[3:0]), .en(decoder_2_out7), .clk(clk), .Q(seven_seg[23:20]));  // open: clr
  buf or_7 (freeze, 1'b0);  // OR_Gate
  Multiplexer #(.enable("false"), .select(4), .width(8)) multiplexer_15 (
    .in0(A), .in1(multiplexer_14_out), .in2(H), .in3(L), .in4(C0), .in5(C1), .in6(mem), .in7(PC[7:0]),
    .in8(PC[15:8]), .in9(port_in), .out(multiplexer_15_out), .sel(read_sel));  // open: in10, in11, in12, in13, in14, in15
  // Probe on multiplexer_15_out
  Adder adder_5 (.a(multiplexer_15_out), .b(8'h1), .out(adder_5_out), .cout(adder_5_cout[2]));  // open: cin
  Subtractor subtractor_2 (
    .a(multiplexer_15_out), .b(8'h1), .out(subtractor_2_out), .bout(subtractor_2_bout[2]));  // open: bin
  alu alu_1 (
    .mode(mode), .A(A), .operand(multiplexer_15_out), .flags_in(F), .result(alu_1_result),
    .flags_out(alu_1_flags_out));
  Comparator #(.mode("unsigned")) comparator_5 (.a(data), .b({8{1'b0}}), .eq(adder_5_cout[3]));  // open: gt, lt
  Subtractor #(.width(5)) subtractor_3 (.a(C0[4:0]), .b(5'b00010), .out(subtractor_3_out));  // open: bin, bout
  Subtractor #(.width(5)) subtractor_4 (.a(C0[4:0]), .b(5'b10100), .out(subtractor_4_out));  // open: bin, bout
  Multiplexer #(.enable("false"), .select(2), .width(4)) multiplexer_16 (
    .in0(alu_1_flags_out), .in1({comparator_7_eq[3], F[2:0]}), .in2({adder_5_cout, F[1:0]}),
    .in3({adder_5_cout[3], subtractor_2_bout[2], F[1:0]}), .out(F_val), .sel(write_op_sel));
  Multiplexer #(.enable("false"), .select(3), .width(4)) multiplexer_17 (
    .in0(seven_seg[3:0]), .in1(seven_seg[7:4]), .in2(seven_seg[11:8]), .in3(seven_seg[15:12]),
    .in4(seven_seg[19:16]), .in5(seven_seg[23:20]), .out(multiplexer_17_out), .sel(subtractor_3_out[2:0]));  // open: in6, in7
  Shifter #(.width(10)) shifter_4 (.in(10'h1), .\dist (subtractor_4_out[3:0]), .out(shifter_4_out));
  Random random_1 (.next(clk), .clk(clk), .out(random_1_out));  // open: clr
  Multiplexer #(.enable("false"), .select(2), .width(8)) multiplexer_18 (
    .in0(alu_1_result), .in1(multiplexer_15_out), .in2(adder_5_out), .in3(subtractor_2_out), .out(data),
    .sel(write_op_sel));
  assign bit_extender_6_out = {{4{1'b0}}, multiplexer_17_out};  // Bit_Extender bit_extender_6
  assign and_4_out = shifter_4_out & switches;  // AND_Gate and_4, 10 bits wide
  Comparator #(.mode("unsigned"), .width(10)) comparator_6 (
    .a(and_4_out), .b({10{1'b0}}), .gt(comparator_6_gt));  // open: eq, lt
  Comparator comparator_7 (.a(data), .b({8{1'b0}}), .eq(comparator_7_eq[3]));  // open: gt, lt
  // Probe on data
  assign bit_extender_7_out = {{7{1'b0}}, btn0};  // Bit_Extender bit_extender_7
  assign bit_extender_8_out = {{7{1'b0}}, btn1};  // Bit_Extender bit_extender_8
  assign bit_extender_9_out = {{7{1'b0}}, comparator_6_gt};  // Bit_Extender bit_extender_9
  Multiplexer #(.enable("false"), .select(5), .width(8)) multiplexer_19 (
    .in0({8{1'b0}}), .in1({8{1'b0}}), .in2(bit_extender_6_out), .in3(bit_extender_6_out),
    .in4(bit_extender_6_out), .in5(bit_extender_6_out), .in6(bit_extender_6_out), .in7(bit_extender_6_out),
    .in8(bit_extender_7_out), .in9(bit_extender_8_out), .in10({8{1'b0}}), .in11({8{1'b0}}), .in12({8{1'b0}}),
    .in13({8{1'b0}}), .in14({8{1'b0}}), .in15({8{1'b0}}), .in16({8{1'b0}}), .in17({8{1'b0}}),
    .in18({8{1'b0}}), .in19({8{1'b0}}), .in20(bit_extender_9_out), .in21(bit_extender_9_out),
    .in22(bit_extender_9_out), .in23(bit_extender_9_out), .in24(bit_extender_9_out),
    .in25(bit_extender_9_out), .in26(bit_extender_9_out), .in27(bit_extender_9_out),
    .in28(bit_extender_9_out), .in29(bit_extender_9_out), .in30({8{1'b0}}), .in31({8{1'b0}}),
    .out(multiplexer_19_out), .sel(C0[4:0]));
  Multiplexer #(.enable("false"), .select(5), .width(8)) multiplexer_20 (
    .in0({8{1'b0}}), .in1({8{1'b0}}), .in2({8{1'b0}}), .in3({8{1'b0}}), .in4({8{1'b0}}), .in5({8{1'b0}}),
    .in6({8{1'b0}}), .in7({8{1'b0}}), .in8({8{1'b0}}), .in9({8{1'b0}}), .in10({8{1'b0}}), .in11({8{1'b0}}),
    .in12({8{1'b0}}), .in13({8{1'b0}}), .in14({8{1'b0}}), .in15({8{1'b0}}), .in16({8{1'b0}}),
    .in17({8{1'b0}}), .in18({8{1'b0}}), .in19({8{1'b0}}), .in20({8{1'b0}}), .in21({8{1'b0}}),
    .in22({8{1'b0}}), .in23({8{1'b0}}), .in24({8{1'b0}}), .in25({8{1'b0}}), .in26({8{1'b0}}),
    .in27({8{1'b0}}), .in28({8{1'b0}}), .in29({8{1'b0}}), .in30({8{1'b0}}), .in31({8{1'b0}}),
    .out(multiplexer_20_out), .sel(C0[4:0]));
  Multiplexer #(.enable("false"), .select(5), .width(8)) multiplexer_21 (
    .in0({8{1'b0}}), .in1({8{1'b0}}), .in2({8{1'b0}}), .in3({8{1'b0}}), .in4({8{1'b0}}), .in5({8{1'b0}}),
    .in6({8{1'b0}}), .in7({8{1'b0}}), .in8({8{1'b0}}), .in9({8{1'b0}}), .in10({8{1'b0}}), .in11({8{1'b0}}),
    .in12({8{1'b0}}), .in13({8{1'b0}}), .in14({8{1'b0}}), .in15({8{1'b0}}), .in16({8{1'b0}}),
    .in17({8{1'b0}}), .in18({8{1'b0}}), .in19({8{1'b0}}), .in20({8{1'b0}}), .in21({8{1'b0}}),
    .in22({8{1'b0}}), .in23({8{1'b0}}), .in24({8{1'b0}}), .in25({8{1'b0}}), .in26({8{1'b0}}),
    .in27({8{1'b0}}), .in28({8{1'b0}}), .in29(random_1_out), .in30({8{1'b0}}), .in31({8{1'b0}}),
    .out(multiplexer_21_out), .sel(C0[4:0]));
  // Probe on C0[4:0]
  // Probe on C0[6:5]
  Multiplexer #(.enable("false"), .select(2), .width(8)) multiplexer_22 (
    .in0(multiplexer_19_out), .in1(multiplexer_20_out), .in2(multiplexer_21_out), .in3({8{1'b0}}),
    .out(port_in), .sel(C0[6:5]));
  // Probe on port_in

  // Other names for the same wires on the sheet: reg_sel[1:0] = cond; mode_1 = mode[0]; mode_2[1:0] = mode[1:0]

  // Notes on the sheet:
  //   contents of Microcode (hex, n*v repeats v):
  //   400000 6*0 530164 5*0 110464 110564 430167 0 0 0 430166 5*0 110464 110564 410617 0 0 0 410616 5*0
  //   110264 510364 4*0 110464 430194 4*0 110464 410714 0 0 0 430118 5*0 43011c 5*0 30338 41030 430228 0 0
  //   0 3033c 41834 43022c 4*0 110464 430040 0 0 0 430010 6*0 110464 430840 0 0 0 430810 6*0 110464 431040
  //   0 0 0 431010 6*0 110464 431840 0 0 0 431810 6*0 110464 432040 0 0 0 432010 6*0 110464 432840 0 0 0
  //   432810 6*0 110464 433040 0 0 0 433010 6*0 110464 423840 0 0 0 423810 6*0 110464 110564 600800 0 0
  //   600000 6*0 201064 500000 4*0 110464 40800 601044 0 0 0 110464 40000 601044 0 0 0 10404 430194 4*0
  //   10404 410714 0 0 0 4000 410615 5*0 41c165 5*0 110464 114564 14675 10685 600800 0 1c465 1c565 600800
  //   0 0 80000
  //   contents of Program (hex, n*v repeats v):
  //   74 0 13 50 72 65 73 73 65 64 20 42 75 74 74 6f 6e 20 0 4 7 34 16 89 44 16 34 c 8d 44 c 28 85 f3 1c
  //   14 1d 8 59 20 a 1c 15 1d 9 61 20 b 4 9 24 18 80 1 2c 30 28 89 80 1b d 84 18 5 3 21 1 10 80 2 9 80 2
  //   4 30 44 8 39 20 0 8 80 2 5 a 21 0 89 15 6c 8 84 da 4 7 10 80 2 88 24 10 80 3 6c a 8 80 2 9 80 3 81 9
  //   5 0 8d 28 6c 2 85 e6 24 8d 7c 96
endmodule

module alu (
  input  [2:0] mode,
  input  [7:0] A,
  input  [7:0] operand,
  input  [3:0] flags_in,
  output [7:0] result,
  output [3:0] flags_out
);

  wire adder_1_cout, adder_2_cout, comparator_1_lt, comparator_2_lt, subtractor_1_bout, subtractor_2_bout,
       xnor_1_out, xor_2_out;
  wire [1:0] and_2_out;
  wire [7:0] adder_1_out, adder_2_out, and_1_out, or_1_out, subtractor_1_out, subtractor_2_out, xor_1_out;

  Comparator comparator_1 (.a(A), .b({8{1'b0}}), .lt(comparator_1_lt));  // open: gt, eq
  Comparator comparator_2 (.a(operand), .b({8{1'b0}}), .lt(comparator_2_lt));  // open: gt, eq
  Multiplexer #(.enable("false"), .select(3), .width(2)) multiplexer_1 (
    .in0(and_2_out), .in1(and_2_out), .in2(and_2_out), .in3(and_2_out), .in4(and_2_out), .in5(flags_in[1:0]),
    .in6(flags_in[1:0]), .in7(flags_in[1:0]), .out(flags_out[1:0]), .sel(mode));
  Adder adder_1 (.a(A), .b(operand), .out(adder_1_out), .cout(adder_1_cout));  // open: cin
  Adder adder_2 (.a(A), .b(operand), .out(adder_2_out), .cin(flags_in[2]), .cout(adder_2_cout));
  Subtractor subtractor_1 (.a(A), .b(operand), .out(subtractor_1_out), .bout(subtractor_1_bout));  // open: bin
  Subtractor subtractor_2 (.a(A), .b(operand), .out(subtractor_2_out), .bin(flags_in[2]), .bout(subtractor_2_bout));
  assign and_1_out = A & operand;  // AND_Gate and_1, 8 bits wide
  assign or_1_out = A | operand;  // OR_Gate or_1, 8 bits wide
  assign xor_1_out = A ^ operand;  // XOR_Gate xor_1, 8 bits wide
  xnor xnor_1 (xnor_1_out, comparator_1_lt, comparator_2_lt);
  and and_2 (and_2_out[0], xnor_1_out, xor_2_out);
  Multiplexer #(.enable("false"), .select(3)) multiplexer_2 (
    .in0(adder_1_cout), .in1(adder_2_cout), .in2(subtractor_1_bout), .in3(subtractor_2_bout),
    .in4(flags_in[2]), .in5(flags_in[2]), .in6(flags_in[2]), .in7(subtractor_1_bout), .out(flags_out[2]),
    .sel(mode));
  xor xor_2 (xor_2_out, comparator_2_lt, and_2_out[1]);
  Multiplexer #(.enable("false"), .select(3), .width(8)) multiplexer_3 (
    .in0(adder_1_out), .in1(adder_2_out), .in2(subtractor_1_out), .in3(subtractor_2_out), .in4(and_1_out),
    .in5(or_1_out), .in6(xor_1_out), .in7(subtractor_1_out), .out(result), .sel(mode));
  Comparator comparator_3 (.a(result), .b({8{1'b0}}), .eq(flags_out[3]), .lt(and_2_out[1]));  // open: gt

  // Notes on the sheet:
  //   ADD
  //   ADC
  //   SUB
  //   SBC
  //   AND
  //   OR
  //   XOR
endmodule
